# Fritzing sketch FuelCellBoard (saved by Fritzing 0.9.4)
circuit board: 4.8cm x 7.4cm
breadboards: 1

parts:
  DFRobot_DFPlayer_Mini1 = DFRobot DFPlayer Mini [part_number=DFR0299]
  SP1 = SPEAKER [package=pcb_mount_speaker]  # not connected
  R1 = Resistor [tolerance=±5% resistance=10 package=THT]
  Speaker = female pin header, 3 pins [form="♀ (female)"]
  Arduino_Micro = Arduino Micro (Rev3)
  Vol = Trimmer Potentiometer [maximum_resistance=100kΩ package=THT]
  Power_5v = female pin header, 2 pins [form="♀ (female)"]
  Output = female pin header, 3 pins [form="♀ (female)"]
  Power_VIN = female pin header, 2 pins [form="♀ (female)"]
  Part1 = Arduino Uno (Rev3)  # not connected
  Input = female pin header, 3 pins [form="♀ (female)"]
  R13 = Resistor [tolerance=±5% resistance=220 package=THT]
  R12 = Resistor [tolerance=±5% resistance=220 package=THT]
  R11 = Resistor [tolerance=±5% resistance=220 package=THT]

nets:
  VCC: DFRobot_DFPlayer_Mini1.VCC, Arduino_Micro.5V, Vol.leg2, Power_5v.pin2
  N1: DFRobot_DFPlayer_Mini1.RX, R1.Pin_1
  N2: DFRobot_DFPlayer_Mini1.TX, Arduino_Micro.D10_PWM/A10
  N3: DFRobot_DFPlayer_Mini1.SPK_1, Speaker.pin1
  N4: DFRobot_DFPlayer_Mini1.GND-1, DFRobot_DFPlayer_Mini1.GND-2, Speaker.pin2, Arduino_Micro.GND, Vol.leg1, Power_5v.pin1, Output.pin3, Power_VIN.pin1
  N5: DFRobot_DFPlayer_Mini1.SPK_2, Speaker.pin3
  N6: DFRobot_DFPlayer_Mini1.BUSY, Arduino_Micro.D3/SCL
  N7: R1.Pin_0, Arduino_Micro.D11_PWM
  N8: Arduino_Micro.D5_PWM, Input.pin3, R13.Pin_1
  N9: Arduino_Micro.D6_PWM/A7, Input.pin2, R12.Pin_1
  N10: Arduino_Micro.D7, Input.pin1, R11.Pin_1
  N11: Arduino_Micro.D8_PWM/A8, Output.pin2
  N12: Arduino_Micro.D9_PWM/A9, Output.pin1
  N13: Arduino_Micro.VIN, Power_VIN.pin2
  N14: Arduino_Micro.A5, Vol.wiper
  N15: R13.Pin_0, R12.Pin_0, R11.Pin_0

notes:
  -
  +
